// Digital circuit sj_digital.dig as structural Verilog
module sj_digital (
  input  clock50Mhz,
  input  [41:0] dreqo,
  input  drspo,
  output left,
  output right,
  output [34:0] drspi,
  output dreqi
);

  wire a__clk, and_1_out, and_2_out, and_4_out, and_5_out, and_6_out, clock50Mhz_t, delay8_ovf, keyboard_av,
       mem_base_eq, mem_read, mem_write, or_1_out, p1__button1, p1__button2, p1__button3, p1__button4,
       p1__button5, p1__button6, p1__down, p1__left, p1__right, p1__select, p1__start, p1__up, p2__button1,
       p2__button2, p2__button3, p2__button4, p2__button5, p2__button6, p2__down, p2__left, p2__right,
       p2__select, p2__start, p2__up, register_1_q, resetn, strobe, v__b, v__clk, v__de, v__g, v__hs, v__r,
       v__vs, v__x, v__y, wb__ack, wb__adr, wb__dat__slave, wb__stb;
  wire [7:0] key_d;
  wire [15:0] keyboard_d, led, switch;
  wire [31:0] mem_addr, mem_d_in, mem_d_out;
  wire [31:24] wb__addr;
  wire [63:0] seg;

  Button button_1 (.out(p1__up));
  Button button_2 (.out(p1__left));
  Button button_3 (.out(p1__down));
  Button button_4 (.out(p2__up));
  Button button_5 (.out(p2__left));
  Button button_6 (.out(p2__down));
  Button button_7 (.out(p1__right));
  Button button_8 (.out(p2__right));
  Reset u_resetn (.out(resetn));
  Button button_9 (.out(p1__select));
  Button button_10 (.out(p1__button1));
  Button button_11 (.out(p1__button2));
  Button button_12 (.out(p1__button3));
  Button button_13 (.out(p1__button4));
  Button button_14 (.out(p1__button5));
  Button button_15 (.out(p1__button6));
  Button button_16 (.out(p2__select));
  Button button_17 (.out(p2__button1));
  Button button_18 (.out(p2__button2));
  Button button_19 (.out(p2__button3));
  Button button_20 (.out(p2__button4));
  Button button_21 (.out(p2__button5));
  Button button_22 (.out(p2__button6));
  Button button_23 (.out(p1__start));
  Button button_24 (.out(p2__start));
  and and_1 (and_1_out, wb__addr[28], wb__addr[29], wb__addr[30], wb__addr[31]);
  and and_2 (and_2_out, and_1_out, wb__stb);
  Demultiplexer #(.Selector_Bits(4)) demultiplexer_1 (
    .sel(wb__addr[27:24]), .in(and_2_out));  // open: out_0, out_1, out_2, out_3, out_4, out_5, out_6, out_7, out_8, out_9, out_10, out_11, out_12, out_13, out_14, out_15
  // vg vg_1: pin names not known; wires that end beside it: clock50Mhz, resetn, p1__select, p1__start, p1__up, p1__down, p1__left, p1__right, p1__button1, p1__button2, p1__button3, p1__button4, p1__button5, p1__button6, p2__select, p2__start, p2__up, p2__down, p2__left, p2__right, p2__button1, p2__button2, p2__button3, p2__button4, p2__button5, p2__button6, switch, wb__dat__slave, wb__ack, dreqo[0], dreqo[7:1], v__r, v__g, v__b, v__vs, v__hs, v__clk, v__x, v__y, v__de, left, right, a__clk, led, seg, wb__adr
  // And and_3 has open pins: In_1=and_1_out, In_2=wb__stb, out=open
  Seven_Seg seven_seg_1 (
    .a(seg[63]), .b(seg[62]), .c(seg[61]), .d(seg[60]), .e(seg[59]), .f(seg[58]), .g(seg[57]), .dp(seg[56]));
  VGA video (.R(v__r), .G(v__g), .B(v__b), .H(v__hs), .V(v__vs), .C(v__clk));
  DipSwitch sw0 (.out(switch[0]));
  DipSwitch sw1 (.out(switch[1]));
  DipSwitch sw2 (.out(switch[2]));
  DipSwitch sw3 (.out(switch[3]));
  DipSwitch sw4 (.out(switch[4]));
  DipSwitch sw5 (.out(switch[5]));
  DipSwitch sw6 (.out(switch[6]));
  DipSwitch sw7 (.out(switch[7]));
  DipSwitch sw8 (.out(switch[8]));
  DipSwitch sw9 (.out(switch[9]));
  DipSwitch sw10 (.out(switch[10]));
  DipSwitch sw11 (.out(switch[11]));
  DipSwitch sw12 (.out(switch[12]));
  DipSwitch sw13 (.out(switch[13]));
  DipSwitch sw14 (.out(switch[14]));
  DipSwitch sw15 (.out(switch[15]));
  Seven_Seg seven_seg_2 (
    .a(seg[55]), .b(seg[54]), .c(seg[53]), .d(seg[52]), .e(seg[51]), .f(seg[50]), .g(seg[49]), .dp(seg[48]));
  and and_4 (and_4_out, mem_write, mem_base_eq);
  and and_5 (and_5_out, mem_read, mem_base_eq);
  Comparator #(.Bits(16)) mem_base (.a(mem_addr[31:16]), .b({16{1'b0}}), .eq(mem_base_eq));  // open: gt, lt
  or or_1 (or_1_out, and_6_out, delay8_ovf);
  Seven_Seg seven_seg_3 (
    .a(seg[47]), .b(seg[46]), .c(seg[45]), .d(seg[44]), .e(seg[43]), .f(seg[42]), .g(seg[41]), .dp(seg[40]));
  Keyboard keyboard (.C(clock50Mhz), .en(and_6_out), .D(keyboard_d), .av(keyboard_av));
  and and_6 (and_6_out, keyboard_av, ~register_1_q);  // And
  LED led0 (.in(led[0]));
  LED led1 (.in(led[1]));
  LED led2 (.in(led[2]));
  LED led3 (.in(led[3]));
  LED led4 (.in(led[4]));
  LED led5 (.in(led[5]));
  LED led6 (.in(led[6]));
  LED led7 (.in(led[7]));
  LED led8 (.in(led[8]));
  LED led9 (.in(led[9]));
  LED led10 (.in(led[10]));
  LED led11 (.in(led[11]));
  LED led12 (.in(led[12]));
  LED led13 (.in(led[13]));
  LED led14 (.in(led[14]));
  LED led15 (.in(led[15]));
  Seven_Seg seven_seg_4 (
    .a(seg[39]), .b(seg[38]), .c(seg[37]), .d(seg[36]), .e(seg[35]), .f(seg[34]), .g(seg[33]), .dp(seg[32]));
  RAMDualPort #(.AddrBits(16), .Bits(32)) exMem (
    .A(mem_addr[15:0]), .Din(mem_d_in), .str(and_4_out), .C(clock50Mhz_t), .ld(and_5_out), .D(mem_d_out));
  Register register_1 (.D(and_6_out), .C(clock50Mhz), .en(or_1_out), .Q(register_1_q));
  Counter #(.Bits(3)) delay8 (.en(register_1_q), .C(clock50Mhz), .clr(1'b0), .ovf(delay8_ovf));  // open: out
  Seven_Seg seven_seg_5 (
    .a(seg[31]), .b(seg[30]), .c(seg[29]), .d(seg[28]), .e(seg[27]), .f(seg[26]), .g(seg[25]), .dp(seg[24]));
  Register #(.Bits(8)) lastKey (.D({1'b0, keyboard_d[6:0]}), .C(clock50Mhz), .en(and_6_out), .Q(key_d));
  D_FF d_ff_1 (.D(register_1_q), .C(clock50Mhz), .Q(strobe));  // open: nQ
  Seven_Seg seven_seg_6 (
    .a(seg[23]), .b(seg[22]), .c(seg[21]), .d(seg[20]), .e(seg[19]), .f(seg[18]), .g(seg[17]), .dp(seg[16]));
  Seven_Seg seven_seg_7 (
    .a(seg[15]), .b(seg[14]), .c(seg[13]), .d(seg[12]), .e(seg[11]), .f(seg[10]), .g(seg[9]), .dp(seg[8]));
  Seven_Seg seven_seg_8 (
    .a(seg[7]), .b(seg[6]), .c(seg[5]), .d(seg[4]), .e(seg[3]), .f(seg[2]), .g(seg[1]), .dp(seg[0]));

  // Other names for the same wires on the sheet: a__left = left; a__right = right; dmi__req__ready = dreqi;
  //   dmi__rsp__data[31:0] = drspi[32:1]; dmi__rsp__op[1:0] = drspi[34:33]; dmi__rsp__ready = drspo;
  //   dmi__rsp__valid = drspi[0]; dmi__req__valid = dreqo[0]; dmi__req__address[6:0] = dreqo[7:1];
  //   dmi__req__data[31:0] = dreqo[39:8]; dmi__req__op[1:0] = dreqo[41:40]

  // Notes on the sheet:
  //   clock50Mhz: Hz: 2147483647
  //   Depuração
  //   sistema
  //   Jogador
  //   Wishbone
  //   AV
  //   Entradas e Saídas Simples
  //   Memória Externa
  //   Teclado
  //   256KB (64K Words) mapped  from
  //   0x00000000  to
  //   0x0000FFFF
  //   Patch circuit for other options
endmodule
